// Logisim project Chips.circ as structural Verilog: 8 circuits, main circuit XL74LS04
module XL74LS04 (
  input  [5:0] A,
  output [5:0] Y
);

  assign Y = ~A;  // NOT_Gate not_1, 6 bits wide
endmodule

module XL74LS08 (
  input  [3:0] A,
  input  [3:0] B,
  output [3:0] Y
);

  assign Y = A & B;  // AND_Gate and_1, 4 bits wide
endmodule

module XL74LS139 (
  input  [1:0] nG,
  input  [1:0] A,
  input  [1:0] B,
  output [1:0] Y0,
  output [1:0] Y1,
  output [1:0] Y2,
  output [1:0] Y3
);

  wire [1:0] not_1_out, not_2_out, not_3_out, not_4_out, not_5_out;

  assign not_1_out = ~nG;  // NOT_Gate not_1, 2 bits wide
  assign not_2_out = ~A;  // NOT_Gate not_2, 2 bits wide
  assign not_3_out = ~B;  // NOT_Gate not_3, 2 bits wide
  assign not_4_out = ~not_2_out;  // NOT_Gate not_4, 2 bits wide
  assign not_5_out = ~not_3_out;  // NOT_Gate not_5, 2 bits wide
  assign Y0 = ~(not_2_out & not_3_out & not_1_out);  // NAND_Gate nand_1, 2 bits wide
  assign Y1 = ~(not_1_out & not_3_out & not_4_out);  // NAND_Gate nand_2, 2 bits wide
  assign Y2 = ~(not_1_out & not_2_out & not_5_out);  // NAND_Gate nand_3, 2 bits wide
  assign Y3 = ~(not_1_out & not_4_out & not_5_out);  // NAND_Gate nand_4, 2 bits wide
endmodule

module SN74LS193DR (
  input  [3:0] D,
  input  MR,
  input  nPL,
  input  CPD,
  input  CPU,
  output nTCD,
  output [3:0] out_7,
  output nTCU
);

  wire and_1_out, and_2_out, and_3_out, and_4_out, comparator_1_eq, comparator_2_eq, not_1_out, or_1_out,
       or_2_out, or_3_out, xor_1_out;

  not not_1 (not_1_out, nPL);
  and and_1 (and_1_out, ~not_1_out, ~CPD, CPU);  // AND_Gate
  or or_1 (or_1_out, not_1_out, and_1_out);
  xor xor_1 (xor_1_out, CPU, CPD);
  and and_2 (and_2_out, ~not_1_out, xor_1_out);  // AND_Gate
  and and_3 (and_3_out, ~not_1_out, and_2_out);  // AND_Gate
  and and_4 (and_4_out, not_1_out, or_2_out);
  or or_2 (or_2_out, CPU, CPD);
  or or_3 (or_3_out, and_3_out, and_4_out);
  Counter #(.width(4), .max('hf)) counter_1 (
    .load(or_1_out), .D(D), .count(and_2_out), .Q(out_7), .clk(or_3_out), .clr(MR));  // open: carry
  Comparator #(.width(4)) comparator_1 (.a(4'b0000), .b(out_7), .eq(comparator_1_eq));  // open: gt, lt
  Comparator #(.width(4)) comparator_2 (.a(out_7), .b(4'b1111), .eq(comparator_2_eq));  // open: gt, lt
  nand nand_1 (nTCD, ~not_1_out, ~CPD, CPU, comparator_1_eq);  // NAND_Gate
  nand nand_2 (nTCU, comparator_2_eq, ~not_1_out, CPD, ~CPU);  // NAND_Gate
endmodule

module XL74LS00 (
  input  [3:0] A,
  input  [3:0] B,
  output [3:0] Y
);

  assign Y = ~(A & B);  // NAND_Gate nand_1, 4 bits wide
endmodule

module MC14490DWG (
  input  [3:0] In,
  input  OSC_In,
  output [3:0] Out,
  output OSC_OUT
);

  wire comparator_1_gt;

  assign Out = In & {4{OSC_In}};  // AND_Gate and_1, 4 bits wide
  Comparator #(.width(4)) comparator_1 (.a(In), .b(4'b0000), .gt(comparator_1_gt));  // open: eq, lt
  and and_2 (OSC_OUT, OSC_In, comparator_1_gt);
endmodule

module LP3470A293DBVR (
  output RST_num
);

  wire and_1_out, clock_1_out, comparator_1_eq, d_ff_1_q, d_ff_2_qn;
  wire [3:0] counter_1_q, demultiplexer_1_out2;

  and and_1 (and_1_out, clock_1_out, ~d_ff_1_q);  // AND_Gate
  Clock clock_1 (.out(clock_1_out));
  Counter #(.width(4), .max('hf)) counter_1 (.Q(counter_1_q), .clk(and_1_out));  // open: load, D, count, carry, clr
  Demultiplexer #(.select(4), .width(4), .enable("false")) demultiplexer_1 (
    .out2(demultiplexer_1_out2), .in(4'b1111), .sel(counter_1_q));  // open: out0, out1, out3, out4, out5, out6, out7, out8, out9, out10, out11, out12, out13, out14, out15
  Comparator #(.width(4)) comparator_1 (.a(4'b1111), .b(demultiplexer_1_out2), .eq(comparator_1_eq));  // open: gt, lt
  D_Flip_Flop d_ff_1 (.clk(comparator_1_eq), .D(1'b1), .Q(d_ff_1_q), .en(1'b1));  // open: Qn, preset, reset
  D_Flip_Flop d_ff_2 (
    .clk(clock_1_out), .D(comparator_1_eq), .Qn(d_ff_2_qn), .en(comparator_1_eq));  // open: Q, preset, reset
  nand nand_1 (RST_num, d_ff_2_qn, comparator_1_eq);
endmodule

module _74HC74_653 (
  input  [1:0] CP,
  input  [1:0] D,
  input  [1:0] SD_num,
  input  [1:0] RD_num,
  output [1:0] Q,
  output [1:0] Q_num
);

  wire [1:0] not_1_out, not_2_out;

  assign not_1_out = ~SD_num;  // NOT_Gate not_1, 2 bits wide
  assign not_2_out = ~RD_num;  // NOT_Gate not_2, 2 bits wide
  D_Flip_Flop d_ff_1 (
    .clk(CP[0]), .D(D[0]), .Q(Q[0]), .Qn(Q_num[0]), .preset(not_1_out[0]), .en(1'b1), .reset(not_2_out[0]));
  D_Flip_Flop d_ff_2 (
    .clk(CP[1]), .D(D[1]), .Q(Q[1]), .Qn(Q_num[1]), .preset(not_1_out[1]), .en(1'b1), .reset(not_2_out[1]));
endmodule
