// Logisim project Computer.circ as structural Verilog: 6 circuits, main circuit main
module main (
  input  in_1,
  input  nWE,
  input  nOE
);

  wire bus_control_logic_1_pass_tru_num, bus_control_logic_2_pass_tru_num, CLK, CLK_HS, CLK_LS, CLK_num,
       clock_1_out, HALT_LED, hex_output_1_d0_num, hex_output_1_d1_num, MODE0_LED, MODE1_LED, MODE2_LED,
       MODE_SW, nand_1_out, nand_2_out, nand_3_out, not_1_out, not_2_out, not_3_out, Power_Switch, PS_ON_num,
       PULSE_SW, Reset_Switch, RST;
  wire [0:0] undriven_2;
  wire [3:0] Control, controlled_buffer_1_out, controlled_buffer_2_out, controlled_buffer_3_out,
       controlled_buffer_4_out, hex_output_1_b, undriven;
  wire [15:0] ADDR, BUS, bus_control_logic_1_address_bus_2, bus_control_logic_1_control_num,
       bus_control_logic_1_data_bus_2, bus_control_logic_2_address_bus_2, bus_control_logic_2_control_num,
       bus_control_logic_2_data_bus_2;

  Button button_1 (.out(Power_Switch));
  Button button_2 (.out(Reset_Switch));
  Clock #(.highDuration(320), .lowDuration(320)) u_CLK_LS (.out(CLK_LS));
  Clock #(.highDuration(64), .lowDuration(64)) u_CLK_HS (.out(CLK_HS));
  Button button_3 (.out(PULSE_SW));
  Button button_4 (.out(MODE_SW));
  Clock #(.highDuration(16), .lowDuration(16)) clock_1 (.out(clock_1_out));
  LED led_1 (.in(MODE0_LED));
  LED led_2 (.in(MODE1_LED));
  LED led_3 (.in(MODE2_LED));
  LED led_4 (.in(HALT_LED));
  LED led_5 (.in(CLK));
  LED led_6 (.in(CLK_num));
  Hex_Output hex_output_1 (
    .CLK(clock_1_out), .Control({4'b0000, Control}), .Address(ADDR), .Bus(BUS), .G(hex_output_1_b[3]),
    .F(hex_output_1_b[2]), .E(undriven[3]), .D(undriven[2]), .C(undriven[1]), .B(hex_output_1_b[0]),
    .A(hex_output_1_b[1]), .D0_num(hex_output_1_d0_num), .D1_num(hex_output_1_d1_num));  // open: D2_num, D3_num, D4_num, D5_num, D6_num, D7_num, D8_num, D9_num
  nand nand_1 (nand_1_out, nWE, nOE);
  nand nand_2 (nand_2_out, nWE, nand_1_out);
  nand nand_3 (nand_3_out, nand_2_out, nand_2_out);
  Random #(.width(16)) random_1 (.clk(CLK), .out(BUS));  // open: next, clr
  Random #(.width(16)) random_2 (.clk(CLK), .out(ADDR));  // open: next, clr
  assign controlled_buffer_1_out = not_1_out ? hex_output_1_b : 4'bz;  // Controlled_Buffer controlled_buffer_1
  assign controlled_buffer_2_out = not_2_out ? hex_output_1_b : 4'bz;  // Controlled_Buffer controlled_buffer_2
  not not_1 (not_1_out, hex_output_1_d0_num);
  not not_2 (not_2_out, hex_output_1_d1_num);
  assign controlled_buffer_3_out = not_1_out ? undriven : 4'bz;  // Controlled_Buffer controlled_buffer_3
  assign controlled_buffer_4_out = not_2_out ? {undriven[3:1], undriven_2[0]} : 4'bz;  // Controlled_Buffer controlled_buffer_4
  Pull_Resistor pull_resistor_1 (.node({controlled_buffer_2_out, controlled_buffer_1_out}));
  _7_Segment_Display u_7_segment_display_1 (
    .g(controlled_buffer_2_out[3]), .f(controlled_buffer_2_out[2]), .a(controlled_buffer_2_out[1]),
    .b(controlled_buffer_2_out[0]), .e(controlled_buffer_4_out[3]), .d(controlled_buffer_4_out[2]),
    .c(controlled_buffer_4_out[1]), .dp(controlled_buffer_4_out[0]));
  Pull_Resistor pull_resistor_2 (.node({controlled_buffer_4_out, controlled_buffer_3_out}));
  Counter #(.width(4), .max('hf)) counter_1 (.Q(Control), .clk(CLK));  // open: load, D, count, carry, clr
  _7_Segment_Display u_7_segment_display_2 (
    .g(controlled_buffer_1_out[3]), .f(controlled_buffer_1_out[2]), .a(controlled_buffer_1_out[1]),
    .b(controlled_buffer_1_out[0]), .e(controlled_buffer_3_out[3]), .d(controlled_buffer_3_out[2]),
    .c(controlled_buffer_3_out[1]), .dp(controlled_buffer_3_out[0]));
  not not_3 (not_3_out, PS_ON_num);
  Bus_Control_Logic bus_control_logic_1 (
    .Control({4'b0000, Control}), .CTRL_Address(8'h1), .CLK_num(CLK_num), .CLK(CLK), .RST(RST),
    .Data_BUS(BUS), .Address_BUS(ADDR), .Control_num(bus_control_logic_1_control_num),
    .Pass_tru_num(bus_control_logic_1_pass_tru_num), .Data_BUS_2(bus_control_logic_1_data_bus_2),
    .Address_BUS_2(bus_control_logic_1_address_bus_2));
  Bus_Control_Logic bus_control_logic_2 (
    .Control({4'b0000, Control}), .CTRL_Address(8'h9), .CLK_num(CLK_num), .CLK(CLK), .RST(RST),
    .Data_BUS(BUS), .Address_BUS(ADDR), .Control_num(bus_control_logic_2_control_num),
    .Pass_tru_num(bus_control_logic_2_pass_tru_num), .Data_BUS_2(bus_control_logic_2_data_bus_2),
    .Address_BUS_2(bus_control_logic_2_address_bus_2));
  Power___PS_ON power_ps_on_1 (.SW(Power_Switch), .PS_ON_num(PS_ON_num));
  Clock_Control clock_control_1 (
    .CLK_LS(CLK_LS), .CLK_HS(CLK_HS), .Mode_sw(MODE_SW), .Pulse_sw(PULSE_SW), .RST(RST), .HLT(in_1),
    .CLK(CLK), .nCLK(CLK_num), .nManual(MODE0_LED), .nAuto_LS(MODE1_LED), .nAuto_HS(MODE2_LED),
    .Halt(HALT_LED));
  // Probe on bus_control_logic_1_control_num
  // Probe on bus_control_logic_1_pass_tru_num
  // Probe on bus_control_logic_1_data_bus_2
  // Probe on bus_control_logic_1_address_bus_2
  // Probe on bus_control_logic_2_control_num
  // Probe on bus_control_logic_2_pass_tru_num
  // Probe on bus_control_logic_2_data_bus_2
  // Probe on bus_control_logic_2_address_bus_2
  Power___Reset power_reset_1 (.SW(Reset_Switch), .PWR_OK(not_3_out), .RST(RST));

  // Other names for the same wires on the sheet: HLT = in_1

  // Notes on the sheet:
  //   in_1: pull=down
endmodule

module Clock_Control (
  input  CLK_LS,
  input  CLK_HS,
  input  Mode_sw,
  input  Pulse_sw,
  input  RST,
  input  HLT,
  output CLK,
  output nCLK,
  output nManual,
  output nAuto_LS,
  output nAuto_HS,
  output Halt
);

  wire C0, C1, CLK_HLT, CLK_HLT_num, CLK_INT, CLK_NOT_HLT, HLT_num, MODE0_num, MODE1_num, MODE2_num,
       MODE_RST, MODE_RST_num, MODE_TRG, or_1_out, PULSE_TRG, RST_num;
  wire [1:1] undriven, undriven_2, xl74ls139_1_y0, xl74ls139_1_y1, xl74ls139_1_y2, xl74ls139_1_y3;
  wire [2:0] xl74ls08_1_y;
  wire [3:2] mc14490dwg_1_out, sn74ls193dr_1_out_7;
  wire [3:3] undriven_3, undriven_4, xl74ls00_1_y;

  or or_1 (or_1_out, MODE_RST, RST);
  MC14490DWG mc14490dwg_1 (
    .In({2'b00, Mode_sw, Pulse_sw}), .OSC_In(1'b1), .Out({mc14490dwg_1_out, MODE_TRG, PULSE_TRG}));  // open: OSC_OUT
  SN74LS193DR sn74ls193dr_1 (
    .D(4'b1111), .MR(or_1_out), .nPL(RST_num), .CPD(1'b1), .CPU(MODE_TRG),
    .out_7({sn74ls193dr_1_out_7, C1, C0}));  // open: nTCD, nTCU
  XL74LS04 xl74ls04_1 (
    .A({HLT, MODE_RST_num, MODE2_num, MODE1_num, MODE0_num, RST}),
    .Y({HLT_num, MODE_RST, nAuto_HS, nAuto_LS, nManual, RST_num}));
  XL74LS139 xl74ls139_1 (
    .nG(2'b00), .A({undriven[1], C0}), .B({undriven_2[1], C1}), .Y0({xl74ls139_1_y0[1], MODE0_num}),
    .Y1({xl74ls139_1_y1[1], MODE1_num}), .Y2({xl74ls139_1_y2[1], MODE2_num}),
    .Y3({xl74ls139_1_y3[1], MODE_RST_num}));
  or or_2 (CLK, CLK_HLT, CLK_NOT_HLT);
  XL74LS00 xl74ls00_1 (
    .A({undriven_3[3], CLK, CLK_HLT_num, PULSE_TRG}), .B({undriven_4[3], CLK, CLK_HLT_num, HLT}),
    .Y({xl74ls00_1_y[3], nCLK, CLK_HLT, CLK_HLT_num}));
  XL74LS08 xl74ls08_1 (
    .A({HLT_num, nAuto_HS, nAuto_LS, nManual}), .B({CLK_INT, CLK_HS, CLK_LS, PULSE_TRG}),
    .Y({CLK_NOT_HLT, xl74ls08_1_y}));
  or or_3 (CLK_INT, xl74ls08_1_y[0], xl74ls08_1_y[1], xl74ls08_1_y[2]);

  assign Halt = HLT;

  // Other names for the same wires on the sheet: MODE0 = nManual; MODE1 = nAuto_LS; MODE2 = nAuto_HS; CLK_num = nCLK
endmodule

module Power___PS_ON (
  input  SW,
  output PS_ON_num
);

  wire [1:0] n74hc74_653_1_q;
  wire [1:1] lp3470a293dbvr_1_rst_num, n74hc74_653_1_q_num;

  LP3470A293DBVR lp3470a293dbvr_1 (.RST_num(lp3470a293dbvr_1_rst_num[1]));
  _74HC74_653 u_74hc74_653_1 (
    .CP({1'b0, SW}), .D(2'b01), .SD_num(2'b11), .RD_num({2{lp3470a293dbvr_1_rst_num[1]}}),
    .Q(n74hc74_653_1_q), .Q_num({n74hc74_653_1_q_num[1], PS_ON_num}));
endmodule

module Power___Reset (
  input  SW,
  input  PWR_OK,
  output RST
);

  wire [0:0] lp3470a293dbvr_1_rst_num;
  wire [5:0] xl74ls04_1_y;

  LP3470A293DBVR lp3470a293dbvr_1 (.RST_num(lp3470a293dbvr_1_rst_num[0]));
  XL74LS04 xl74ls04_1 (.A({4'b0000, PWR_OK, lp3470a293dbvr_1_rst_num[0]}), .Y(xl74ls04_1_y));
  or or_1 (RST, SW, xl74ls04_1_y[0], xl74ls04_1_y[1]);
endmodule

module Bus_Control_Logic (
  input  [7:0] Control,
  input  [7:0] CTRL_Address,
  input  CLK_num,
  input  CLK,
  input  RST,
  input  [15:0] Data_BUS,
  input  [15:0] Address_BUS,
  output [15:0] Control_num,
  output Pass_tru_num,
  output [15:0] Data_BUS_2,
  output [15:0] Address_BUS_2
);

  wire CTRL_ACTIVE, CTRL_LATCH, CTRL_LATCH_num, CTRL_RESET, CTRL_RESET_num, n74hct85d_653_1_out_6,
       n74hct85d_653_1_out_7, n74hct85d_653_1_out_8, n74hct85d_653_2_out_6, n74hct85d_653_2_out_7,
       n74hct85d_653_2_out_8;
  wire [1:0] n74hc74_653_1_q_num;
  wire [1:1] n74hc74_653_1_q, undriven_3, undriven_4, undriven_5, undriven_7;
  wire [3:0] xl74ls08_1_y_2, xl74ls08_2_y;
  wire [3:2] undriven;
  wire [3:3] undriven_2, xl74ls08_1_y;
  wire [5:3] undriven_6, xl74ls04_1_y;
  wire [7:0] gr_74hc574ts_1_q;

  _74HCT85D_653 u_74hct85d_653_1 (
    .IN(1'b0), .IN_2(1'b1), .IN_3(1'b0), .A(Control[3:0]), .B(CTRL_Address[3:0]),
    .out_8(n74hct85d_653_1_out_8), .out_7(n74hct85d_653_1_out_7), .out_6(n74hct85d_653_1_out_6));
  _74HCT85D_653 u_74hct85d_653_2 (
    .IN(1'b0), .IN_2(1'b1), .IN_3(1'b0), .A(Control[3:0]), .B(4'b1111), .out_8(n74hct85d_653_2_out_8),
    .out_7(n74hct85d_653_2_out_7), .out_6(n74hct85d_653_2_out_6));
  _74HC74_653 u_74hc74_653_1 (
    .CP({undriven_3[1], CLK}), .D({undriven_4[1], CTRL_ACTIVE}), .SD_num({undriven_7[1], CTRL_LATCH_num}),
    .RD_num({undriven_5[1], CTRL_RESET_num}), .Q({n74hc74_653_1_q[1], CTRL_LATCH}),
    .Q_num(n74hc74_653_1_q_num));
  XL74LS04 xl74ls04_1 (
    .A({undriven_6, RST, CTRL_LATCH, CTRL_RESET}),
    .Y({xl74ls04_1_y, undriven[2], CTRL_LATCH_num, CTRL_RESET_num}));
  XL74LS08 xl74ls08_1 (
    .A({undriven, {2{CLK}}}), .B({undriven_2[3], CTRL_RESET_num, CTRL_RESET, CTRL_ACTIVE}),
    .Y({xl74ls08_1_y_2[3], xl74ls08_1_y[3], xl74ls08_1_y_2[1:0]}));
  GR_74HC574TS gr_74hc574ts_1 (.OE_num(1'b0), .CLK(Pass_tru_num), .D({4'b0000, xl74ls08_2_y}), .Q(gr_74hc574ts_1_q));
  XL74LS08 xl74ls08_2 (.A({4{xl74ls08_1_y[3]}}), .B(Data_BUS[3:0]), .Y(xl74ls08_2_y));
  _74HCT85D_653 u_74hct85d_653_3 (
    .IN(n74hct85d_653_1_out_8), .IN_2(n74hct85d_653_1_out_7), .IN_3(n74hct85d_653_1_out_6), .A(Control[7:4]),
    .B(CTRL_Address[7:4]), .out_7(CTRL_ACTIVE));  // open: out_8, out_6
  _74HCT85D_653 u_CTRL_RESET (
    .IN(n74hct85d_653_2_out_8), .IN_2(n74hct85d_653_2_out_7), .IN_3(n74hct85d_653_2_out_6), .A(Control[7:4]),
    .B(4'b1111), .out_7(CTRL_RESET));  // open: out_8, out_6
  or or_1 (Pass_tru_num, xl74ls08_1_y_2[0], xl74ls08_1_y_2[1]);
  SN74LS541DWR sn74ls541dwr_1 (.G1_num(Pass_tru_num), .G2_num(1'b0), .A(Data_BUS[7:0]), .out_4(Data_BUS_2[7:0]));
  SN74LS541DWR sn74ls541dwr_2 (.G1_num(Pass_tru_num), .G2_num(1'b0), .A(Data_BUS[15:8]), .out_4(Data_BUS_2[15:8]));
  SN74LS541DWR sn74ls541dwr_3 (.G1_num(Pass_tru_num), .G2_num(1'b0), .A(Address_BUS[7:0]), .out_4(Address_BUS_2[7:0]));
  SN74LS541DWR sn74ls541dwr_4 (
    .G1_num(Pass_tru_num), .G2_num(1'b0), .A(Address_BUS[15:8]), .out_4(Address_BUS_2[15:8]));
  XL74LS138 xl74ls138_1 (
    .A(gr_74hc574ts_1_q[0]), .B(gr_74hc574ts_1_q[1]), .C(gr_74hc574ts_1_q[2]), .G1(1'b1),
    .G2A_num(gr_74hc574ts_1_q[3]), .G2B_num(1'b0), .Y_num(Control_num[7:0]));
  XL74LS138 xl74ls138_2 (
    .A(gr_74hc574ts_1_q[0]), .B(gr_74hc574ts_1_q[1]), .C(gr_74hc574ts_1_q[2]), .G1(gr_74hc574ts_1_q[3]),
    .G2A_num(1'b0), .G2B_num(1'b0), .Y_num(Control_num[15:8]));
  Pull_Resistor pull_resistor_1 (.node(Data_BUS_2));
  Pull_Resistor pull_resistor_2 (.node(Address_BUS_2));

  // Notes on the sheet:
  //   0xFF = CTRL RESET, Reset all controls
endmodule

module Hex_Output (
  input  CLK,
  input  [7:0] Control,
  input  [15:0] Address,
  input  [15:0] Bus,
  output G,
  output F,
  output E,
  output D,
  output C,
  output B,
  output A,
  output D0_num,
  output D1_num,
  output D2_num,
  output D3_num,
  output D4_num,
  output D5_num,
  output D6_num,
  output D7_num,
  output D8_num,
  output D9_num
);

  wire A_t, B_t, C_t, D_t, Lower_num, RST, RST_num, S0, S0_num, S1, S1_num, S2, S2_num, S3, S3_num, S4,
       S4_num, Upper_num;
  wire [7:0] ROM_ADDR, sn74ls541dwr_1_out_4;
  wire [7:3] xl74ls138_2_y_num;
  wire [7:7] rom_1_data;

  // Probe on ROM_ADDR
  ROM rom_1 (.addr(ROM_ADDR), .data({rom_1_data[7], A, B, C, D, E, F, G}));  // open: sel
  and and_1 (Lower_num, D8_num, D6_num, D4_num, D2_num, D0_num);
  and and_2 (Upper_num, D1_num, D3_num, D5_num, D7_num, D9_num);
  XL74LS138 xl74ls138_1 (
    .A(A_t), .B(B_t), .C(C_t), .G1(1'b1), .G2A_num(D_t), .G2B_num(1'b0),
    .Y_num({D7_num, D6_num, D5_num, D4_num, D3_num, D2_num, D1_num, D0_num}));
  XL74LS138 xl74ls138_2 (
    .A(A_t), .B(B_t), .C(C_t), .G1(D_t), .G2A_num(1'b0), .G2B_num(1'b0),
    .Y_num({xl74ls138_2_y_num, RST_num, D9_num, D8_num}));
  SN74LS193DR sn74ls193dr_1 (
    .D(4'b0000), .MR(RST), .nPL(1'b1), .CPD(1'b1), .CPU(CLK), .out_7({D_t, C_t, B_t, A_t}));  // open: nTCD, nTCU
  SN74LS541DWR sn74ls541dwr_1 (.G1_num(S0_num), .G2_num(1'b0), .A(Control), .out_4(sn74ls541dwr_1_out_4));
  SN74LS541DWR sn74ls541dwr_2 (.G1_num(S1_num), .G2_num(1'b0), .A(Address[7:0]), .out_4(sn74ls541dwr_1_out_4));
  SN74LS541DWR sn74ls541dwr_3 (.G1_num(S2_num), .G2_num(1'b0), .A(Address[15:8]), .out_4(sn74ls541dwr_1_out_4));
  SN74LS541DWR sn74ls541dwr_4 (.G1_num(S3_num), .G2_num(1'b0), .A(Bus[7:0]), .out_4(sn74ls541dwr_1_out_4));
  SN74LS541DWR sn74ls541dwr_5 (.G1_num(S4_num), .G2_num(1'b0), .A(Bus[15:8]), .out_4(sn74ls541dwr_1_out_4));
  Pull_Resistor pull_resistor_1 (.node(sn74ls541dwr_1_out_4));
  xor xor_1 (S1, D2_num, D3_num);
  xor xor_2 (S0, D0_num, D1_num);
  xor xor_3 (S2, D4_num, D5_num);
  xor xor_4 (S3, D6_num, D7_num);
  Pull_Resistor pull_resistor_2 (.node(ROM_ADDR));
  SN74LS541DWR sn74ls541dwr_6 (
    .G1_num(Lower_num), .G2_num(1'b0), .A({4'b0000, sn74ls541dwr_1_out_4[3:0]}), .out_4(ROM_ADDR));
  SN74LS541DWR sn74ls541dwr_7 (
    .G1_num(Upper_num), .G2_num(1'b0), .A({4'b0000, sn74ls541dwr_1_out_4[7:4]}), .out_4(ROM_ADDR));
  xor xor_5 (S4, D8_num, D9_num);
  XL74LS04 xl74ls04_1 (.A({RST_num, S4, S3, S2, S1, S0}), .Y({RST, S4_num, S3_num, S2_num, S1_num, S0_num}));

  // Other names for the same wires on the sheet: ADDR_LH[7:0] = Address[7:0]; ADDR_UH[7:0] = Address[15:8];
  //   BUS_LH[7:0] = Bus[7:0]; BUS_UH[7:0] = Bus[15:8]; CTRL[7:0] = Control

  // Notes on the sheet:
  //   contents of rom_1 (hex, n*v repeats v):
  //   7e 30 6d 79 33 5b 5f 70 7f 7b 77 1f 4e 3d 4f 47
endmodule
