// Logisim project Hex Output Control.circ as structural Verilog: 4 circuits, main circuit main
module Hex_Output_Control (
  input  CLK,
  input  [7:0] Control,
  input  [15:0] Address,
  input  [15:0] Data,
  output [7:0] ROM_ADDR,
  output nSCL,
  output nSAL,
  output nSAU,
  output nSDL,
  output nSDU
);

  wire A, B, C, nRST, RST;
  wire [3:3] sn74ls193dr_1_out_7;
  wire [5:1] undriven, xl74ls04_1_y;
  wire [7:6] xl74ls138_1_y_num;

  XL74LS138 xl74ls138_1 (
    .A(A), .B(B), .C(C), .G1(1'b1), .G2A_num(1'b0), .G2B_num(1'b0),
    .Y_num({xl74ls138_1_y_num, nRST, nSDU, nSDL, nSAU, nSAL, nSCL}));
  SN74LS541DWR sn74ls541dwr_1 (.G1_num(nSCL), .G2_num(1'b0), .A(Control), .out_4(ROM_ADDR));
  SN74LS541DWR sn74ls541dwr_2 (.G1_num(nSAL), .G2_num(1'b0), .A(Address[7:0]), .out_4(ROM_ADDR));
  SN74LS541DWR sn74ls541dwr_3 (.G1_num(nSAU), .G2_num(1'b0), .A(Address[15:8]), .out_4(ROM_ADDR));
  SN74LS541DWR sn74ls541dwr_4 (.G1_num(nSDL), .G2_num(1'b0), .A(Data[7:0]), .out_4(ROM_ADDR));
  SN74LS541DWR sn74ls541dwr_5 (.G1_num(nSDU), .G2_num(1'b0), .A(Data[15:8]), .out_4(ROM_ADDR));
  SN74LS193DR sn74ls193dr_1 (
    .D(4'b0000), .MR(RST), .nPL(1'b1), .CPD(1'b1), .CPU(CLK), .out_7({sn74ls193dr_1_out_7[3], C, B, A}));  // open: nTCD, nTCU
  XL74LS04 xl74ls04_1 (.A({undriven, nRST}), .Y({xl74ls04_1_y, RST}));

  // Other names for the same wires on the sheet: AL[7:0] = Address[7:0]; AU[7:0] = Address[15:8];
  //   Byte[7:0] = ROM_ADDR; CL[7:0] = Control; DL[7:0] = Data[7:0]; DU[7:0] = Data[15:8]
endmodule

module main (
);

  wire clock_1_out, clock_2_out, hex_output_control_1_nsal, hex_output_control_1_nsau,
       hex_output_control_1_nscl, hex_output_control_1_nsdl, hex_output_control_1_nsdu;
  wire [7:0] hex_output_control_1_rom_addr, memory_1_lower, memory_1_upper, random_1_out;
  wire [15:0] random_2_out, random_3_out;

  Clock clock_1 (.out(clock_1_out));
  Clock #(.highDuration(5), .lowDuration(5)) clock_2 (.out(clock_2_out));
  Random random_1 (.clk(clock_2_out), .out(random_1_out));  // open: next, clr
  Random #(.width(16)) random_2 (.clk(clock_2_out), .out(random_2_out));  // open: next, clr
  Random #(.width(16)) random_3 (.clk(clock_2_out), .out(random_3_out));  // open: next, clr
  Hex_Output_Control hex_output_control_1 (
    .CLK(clock_1_out), .Control(random_1_out), .Address(random_2_out), .Data(random_3_out),
    .ROM_ADDR(hex_output_control_1_rom_addr), .nSCL(hex_output_control_1_nscl),
    .nSAL(hex_output_control_1_nsal), .nSAU(hex_output_control_1_nsau), .nSDL(hex_output_control_1_nsdl),
    .nSDU(hex_output_control_1_nsdu));
  Display display_1 (
    .nSCL(hex_output_control_1_nscl), .nSAL(hex_output_control_1_nsal), .nSAU(hex_output_control_1_nsau),
    .nSDL(hex_output_control_1_nsdl), .nSDU(hex_output_control_1_nsdu), .Upper(memory_1_upper),
    .Lower(memory_1_lower));
  Memory memory_1 (.Address(hex_output_control_1_rom_addr), .Upper(memory_1_upper), .Lower(memory_1_lower));
endmodule

module Display (
  input  nSCL,
  input  nSAL,
  input  nSAU,
  input  nSDL,
  input  nSDU,
  input  [7:0] Upper,
  input  [7:0] Lower
);

  wire not_1_out, not_2_out, not_3_out, not_4_out, not_5_out;
  wire [7:0] controlled_buffer_1_out, controlled_buffer_2_out, controlled_buffer_3_out,
       controlled_buffer_4_out, controlled_buffer_5_out, controlled_buffer_6_out, controlled_buffer_7_out,
       controlled_buffer_8_out, controlled_buffer_9_out, controlled_buffer_10_out;

  not not_1 (not_1_out, nSCL);
  not not_2 (not_2_out, nSAL);
  not not_3 (not_3_out, nSAU);
  not not_4 (not_4_out, nSDL);
  not not_5 (not_5_out, nSDU);
  assign controlled_buffer_1_out = not_1_out ? Upper : 8'bz;  // Controlled_Buffer controlled_buffer_1
  assign controlled_buffer_2_out = not_1_out ? Lower : 8'bz;  // Controlled_Buffer controlled_buffer_2
  _7_Segment_Display u_7_segment_display_1 (
    .g(controlled_buffer_1_out[0]), .f(controlled_buffer_1_out[1]), .a(controlled_buffer_1_out[6]),
    .b(controlled_buffer_1_out[5]), .e(controlled_buffer_1_out[2]), .d(controlled_buffer_1_out[3]),
    .c(controlled_buffer_1_out[4]));  // open: dp
  _7_Segment_Display u_7_segment_display_2 (
    .g(controlled_buffer_2_out[0]), .f(controlled_buffer_2_out[1]), .a(controlled_buffer_2_out[6]),
    .b(controlled_buffer_2_out[5]), .e(controlled_buffer_2_out[2]), .d(controlled_buffer_2_out[3]),
    .c(controlled_buffer_2_out[4]));  // open: dp
  assign controlled_buffer_3_out = not_2_out ? Upper : 8'bz;  // Controlled_Buffer controlled_buffer_3
  assign controlled_buffer_4_out = not_2_out ? Lower : 8'bz;  // Controlled_Buffer controlled_buffer_4
  _7_Segment_Display u_7_segment_display_3 (
    .g(controlled_buffer_4_out[0]), .f(controlled_buffer_4_out[1]), .a(controlled_buffer_4_out[6]),
    .b(controlled_buffer_4_out[5]), .e(controlled_buffer_4_out[2]), .d(controlled_buffer_4_out[3]),
    .c(controlled_buffer_4_out[4]));  // open: dp
  _7_Segment_Display u_7_segment_display_4 (
    .g(controlled_buffer_3_out[0]), .f(controlled_buffer_3_out[1]), .a(controlled_buffer_3_out[6]),
    .b(controlled_buffer_3_out[5]), .e(controlled_buffer_3_out[2]), .d(controlled_buffer_3_out[3]),
    .c(controlled_buffer_3_out[4]));  // open: dp
  assign controlled_buffer_5_out = not_3_out ? Upper : 8'bz;  // Controlled_Buffer controlled_buffer_5
  assign controlled_buffer_6_out = not_3_out ? Lower : 8'bz;  // Controlled_Buffer controlled_buffer_6
  _7_Segment_Display u_7_segment_display_5 (
    .g(controlled_buffer_5_out[0]), .f(controlled_buffer_5_out[1]), .a(controlled_buffer_5_out[6]),
    .b(controlled_buffer_5_out[5]), .e(controlled_buffer_5_out[2]), .d(controlled_buffer_5_out[3]),
    .c(controlled_buffer_5_out[4]));  // open: dp
  _7_Segment_Display u_7_segment_display_6 (
    .g(controlled_buffer_6_out[0]), .f(controlled_buffer_6_out[1]), .a(controlled_buffer_6_out[6]),
    .b(controlled_buffer_6_out[5]), .e(controlled_buffer_6_out[2]), .d(controlled_buffer_6_out[3]),
    .c(controlled_buffer_6_out[4]));  // open: dp
  assign controlled_buffer_7_out = not_4_out ? Upper : 8'bz;  // Controlled_Buffer controlled_buffer_7
  assign controlled_buffer_8_out = not_4_out ? Lower : 8'bz;  // Controlled_Buffer controlled_buffer_8
  _7_Segment_Display u_7_segment_display_7 (
    .g(controlled_buffer_8_out[0]), .f(controlled_buffer_8_out[1]), .a(controlled_buffer_8_out[6]),
    .b(controlled_buffer_8_out[5]), .e(controlled_buffer_8_out[2]), .d(controlled_buffer_8_out[3]),
    .c(controlled_buffer_8_out[4]));  // open: dp
  _7_Segment_Display u_7_segment_display_8 (
    .g(controlled_buffer_7_out[0]), .f(controlled_buffer_7_out[1]), .a(controlled_buffer_7_out[6]),
    .b(controlled_buffer_7_out[5]), .e(controlled_buffer_7_out[2]), .d(controlled_buffer_7_out[3]),
    .c(controlled_buffer_7_out[4]));  // open: dp
  assign controlled_buffer_9_out = not_5_out ? Upper : 8'bz;  // Controlled_Buffer controlled_buffer_9
  assign controlled_buffer_10_out = not_5_out ? Lower : 8'bz;  // Controlled_Buffer controlled_buffer_10
  _7_Segment_Display u_7_segment_display_9 (
    .g(controlled_buffer_9_out[0]), .f(controlled_buffer_9_out[1]), .a(controlled_buffer_9_out[6]),
    .b(controlled_buffer_9_out[5]), .e(controlled_buffer_9_out[2]), .d(controlled_buffer_9_out[3]),
    .c(controlled_buffer_9_out[4]));  // open: dp
  _7_Segment_Display u_7_segment_display_10 (
    .g(controlled_buffer_10_out[0]), .f(controlled_buffer_10_out[1]), .a(controlled_buffer_10_out[6]),
    .b(controlled_buffer_10_out[5]), .e(controlled_buffer_10_out[2]), .d(controlled_buffer_10_out[3]),
    .c(controlled_buffer_10_out[4]));  // open: dp

  // Notes on the sheet:
  //   nSCL: pull=up
  //   nSAU: pull=up
  //   nSDU: pull=up
  //   nSDL: pull=up
  //   nSAL: pull=up
endmodule

module Memory (
  input  [7:0] Address,
  output [7:0] Upper,
  output [7:0] Lower
);

  ROM rom_1 (.addr(Address), .data(Upper), .sel(1'b1));
  ROM rom_2 (.addr(Address), .data(Lower), .sel(1'b1));

  // Notes on the sheet:
  //   contents of rom_1 (hex, n*v repeats v):
  //   16*7e 16*30 16*6d 16*79 16*33 16*5b 16*5f 16*70 16*7f 16*7b 16*77 16*1f 16*4e 16*3d 16*4f 16*47
  //   contents of rom_2 (hex, n*v repeats v):
  //   7e 30 6d 79 33 5b 5f 70 7f 7b 77 1f 4e 3d 4f 47 7e 30 6d 79 33 5b 5f 70 7f 7b 77 1f 4e 3d 4f 47 7e
  //   30 6d 79 33 5b 5f 70 7f 7b 77 1f 4e 3d 4f 47 7e 30 6d 79 33 5b 5f 70 7f 7b 77 1f 4e 3d 4f 47 7e 30
  //   6d 79 33 5b 5f 70 7f 7b 77 1f 4e 3d 4f 47 7e 30 6d 79 33 5b 5f 70 7f 7b 77 1f 4e 3d 4f 47 7e 30 6d
  //   79 33 5b 5f 70 7f 7b 77 1f 4e 3d 4f 47 7e 30 6d 79 33 5b 5f 70 7f 7b 77 1f 4e 3d 4f 47 7e 30 6d 79
  //   33 5b 5f 70 7f 7b 77 1f 4e 3d 4f 47 7e 30 6d 79 33 5b 5f 70 7f 7b 77 1f 4e 3d 4f 47 7e 30 6d 79 33
  //   5b 5f 70 7f 7b 77 1f 4e 3d 4f 47 7e 30 6d 79 33 5b 5f 70 7f 7b 77 1f 4e 3d 4f 47 7e 30 6d 79 33 5b
  //   5f 70 7f 7b 77 1f 4e 3d 4f 47 7e 30 6d 79 33 5b 5f 70 7f 7b 77 1f 4e 3d 4f 47 7e 30 6d 79 33 5b 5f
  //   70 7f 7b 77 1f 4e 3d 4f 47 7e 30 6d 79 33 5b 5f 70 7f 7b 77 1f 4e 3d 4f 47
endmodule
