// Logisim project Chips.circ as structural Verilog: 13 circuits, main circuit XL74LS04
module XL74LS04 (
  input  [5:0] A,
  output [5:0] Y
);

  assign Y = ~A;  // NOT_Gate not_1, 6 bits wide
endmodule

module XL74LS08 (
  input  [3:0] A,
  input  [3:0] B,
  output [3:0] Y
);

  assign Y = A & B;  // AND_Gate and_1, 4 bits wide
endmodule

module XL74LS139 (
  input  [1:0] nG,
  input  [1:0] A,
  input  [1:0] B,
  output [1:0] Y0,
  output [1:0] Y1,
  output [1:0] Y2,
  output [1:0] Y3
);

  wire [1:0] not_1_out, not_2_out, not_3_out, not_4_out, not_5_out;

  assign not_1_out = ~nG;  // NOT_Gate not_1, 2 bits wide
  assign not_2_out = ~A;  // NOT_Gate not_2, 2 bits wide
  assign not_3_out = ~B;  // NOT_Gate not_3, 2 bits wide
  assign not_4_out = ~not_2_out;  // NOT_Gate not_4, 2 bits wide
  assign not_5_out = ~not_3_out;  // NOT_Gate not_5, 2 bits wide
  assign Y0 = ~(not_2_out & not_3_out & not_1_out);  // NAND_Gate nand_1, 2 bits wide
  assign Y1 = ~(not_1_out & not_3_out & not_4_out);  // NAND_Gate nand_2, 2 bits wide
  assign Y2 = ~(not_1_out & not_2_out & not_5_out);  // NAND_Gate nand_3, 2 bits wide
  assign Y3 = ~(not_1_out & not_4_out & not_5_out);  // NAND_Gate nand_4, 2 bits wide
endmodule

module SN74LS193DR (
  input  [3:0] D,
  input  MR,
  input  nPL,
  input  CPD,
  input  CPU,
  output nTCD,
  output [3:0] out_7,
  output nTCU
);

  wire and_1_out, and_2_out, and_3_out, and_4_out, comparator_1_eq, comparator_2_eq, not_1_out, or_1_out,
       or_2_out, or_3_out, xor_1_out;

  not not_1 (not_1_out, nPL);
  and and_1 (and_1_out, ~not_1_out, ~CPD, CPU);  // AND_Gate
  or or_1 (or_1_out, not_1_out, and_1_out);
  xor xor_1 (xor_1_out, CPU, CPD);
  and and_2 (and_2_out, ~not_1_out, xor_1_out);  // AND_Gate
  and and_3 (and_3_out, ~not_1_out, and_2_out);  // AND_Gate
  and and_4 (and_4_out, not_1_out, or_2_out);
  or or_2 (or_2_out, CPU, CPD);
  or or_3 (or_3_out, and_3_out, and_4_out);
  Counter #(.width(4), .max('hf)) counter_1 (
    .load(or_1_out), .D(D), .count(and_2_out), .Q(out_7), .clk(or_3_out), .clr(MR));  // open: carry
  Comparator #(.width(4)) comparator_1 (.a(4'b0000), .b(out_7), .eq(comparator_1_eq));  // open: gt, lt
  Comparator #(.width(4)) comparator_2 (.a(out_7), .b(4'b1111), .eq(comparator_2_eq));  // open: gt, lt
  nand nand_1 (nTCD, ~not_1_out, ~CPD, CPU, comparator_1_eq);  // NAND_Gate
  nand nand_2 (nTCU, comparator_2_eq, ~not_1_out, CPD, ~CPU);  // NAND_Gate
endmodule

module XL74LS00 (
  input  [3:0] A,
  input  [3:0] B,
  output [3:0] Y
);

  assign Y = ~(A & B);  // NAND_Gate nand_1, 4 bits wide
endmodule

module MC14490DWG (
  input  [3:0] In,
  input  OSC_In,
  output [3:0] Out,
  output OSC_OUT
);

  wire comparator_1_gt;

  assign Out = In & {4{OSC_In}};  // AND_Gate and_1, 4 bits wide
  Comparator #(.width(4)) comparator_1 (.a(In), .b(4'b0000), .gt(comparator_1_gt));  // open: eq, lt
  and and_2 (OSC_OUT, OSC_In, comparator_1_gt);
endmodule

module LP3470A293DBVR (
  output RST_num
);

  wire and_1_out, clock_1_out, comparator_1_eq, d_ff_1_q, d_ff_2_qn;
  wire [3:0] counter_1_q, demultiplexer_1_out2;

  and and_1 (and_1_out, clock_1_out, ~d_ff_1_q);  // AND_Gate
  Clock clock_1 (.out(clock_1_out));
  Counter #(.width(4), .max('hf)) counter_1 (.Q(counter_1_q), .clk(and_1_out));  // open: load, D, count, carry, clr
  Demultiplexer #(.select(4), .width(4), .enable("false")) demultiplexer_1 (
    .out2(demultiplexer_1_out2), .in(4'b1111), .sel(counter_1_q));  // open: out0, out1, out3, out4, out5, out6, out7, out8, out9, out10, out11, out12, out13, out14, out15
  Comparator #(.width(4)) comparator_1 (.a(4'b1111), .b(demultiplexer_1_out2), .eq(comparator_1_eq));  // open: gt, lt
  D_Flip_Flop d_ff_1 (.clk(comparator_1_eq), .D(1'b1), .Q(d_ff_1_q), .en(1'b1));  // open: Qn, preset, reset
  D_Flip_Flop d_ff_2 (
    .clk(clock_1_out), .D(comparator_1_eq), .Qn(d_ff_2_qn), .en(comparator_1_eq));  // open: Q, preset, reset
  nand nand_1 (RST_num, d_ff_2_qn, comparator_1_eq);
endmodule

module _74HC74_653 (
  input  [1:0] CP,
  input  [1:0] D,
  input  [1:0] SD_num,
  input  [1:0] RD_num,
  output [1:0] Q,
  output [1:0] Q_num
);

  wire [1:0] not_1_out, not_2_out;

  assign not_1_out = ~SD_num;  // NOT_Gate not_1, 2 bits wide
  assign not_2_out = ~RD_num;  // NOT_Gate not_2, 2 bits wide
  D_Flip_Flop d_ff_1 (
    .clk(CP[0]), .D(D[0]), .Q(Q[0]), .Qn(Q_num[0]), .preset(not_1_out[0]), .en(1'b1), .reset(not_2_out[0]));
  D_Flip_Flop d_ff_2 (
    .clk(CP[1]), .D(D[1]), .Q(Q[1]), .Qn(Q_num[1]), .preset(not_1_out[1]), .en(1'b1), .reset(not_2_out[1]));
endmodule

module _74HCT85D_653 (
  input  IN,
  input  IN_2,
  input  IN_3,
  input  [3:0] A,
  input  [3:0] B,
  output out_6,
  output out_7,
  output out_8
);

  wire AB, AB_C, AB_C_num, AB_t, AB_t_t, AL, AL_t, AL_t_t, ALL_LOW, HHL, HHL_t, HHL_t_t, HHL_t_t_t, not_1_out;

  not not_1 (not_1_out, AB_C);
  and and_1 (AB_C, ~ALL_LOW, ~HHL, AB_t);  // AND_Gate
  and and_2 (AB_C_num, ~ALL_LOW, ~HHL, not_1_out);  // AND_Gate
  Comparator #(.width(4), .mode("unsigned")) comparator_1 (.a(A), .b(B), .gt(AB_t_t), .eq(AB_t), .lt(AB));
  Comparator #(.width(4), .mode("unsigned")) comparator_2 (
    .a({1'b0, IN_3, IN_2, IN}), .b(4'b0000), .eq(ALL_LOW));  // open: gt, lt
  and and_3 (AL_t_t, ALL_LOW, 1'b1);
  and and_4 (AL_t, ALL_LOW, 1'b1);
  and and_5 (AL, ALL_LOW, 1'b0);
  assign out_6 = ALL_LOW ? 1'b1 : 1'bz;  // Controlled_Buffer controlled_buffer_1
  assign out_6 = HHL ? 1'b0 : 1'bz;  // Controlled_Buffer controlled_buffer_2
  assign out_6 = AB_C ? IN : 1'bz;  // Controlled_Buffer controlled_buffer_3
  assign out_6 = AB_C_num ? AB_t_t : 1'bz;  // Controlled_Buffer controlled_buffer_4
  assign out_7 = ALL_LOW ? 1'b1 : 1'bz;  // Controlled_Buffer controlled_buffer_5
  assign out_7 = HHL ? 1'b0 : 1'bz;  // Controlled_Buffer controlled_buffer_6
  assign out_7 = AB_C ? IN_2 : 1'bz;  // Controlled_Buffer controlled_buffer_7
  assign out_7 = AB_C_num ? 1'b0 : 1'bz;  // Controlled_Buffer controlled_buffer_8
  assign out_8 = ALL_LOW ? 1'b0 : 1'bz;  // Controlled_Buffer controlled_buffer_9
  assign out_8 = HHL ? 1'b0 : 1'bz;  // Controlled_Buffer controlled_buffer_10
  assign out_8 = AB_C ? IN_3 : 1'bz;  // Controlled_Buffer controlled_buffer_11
  assign out_8 = AB_C_num ? AB : 1'bz;  // Controlled_Buffer controlled_buffer_12
  Comparator #(.width(4), .mode("unsigned")) comparator_3 (
    .a({1'b0, IN_3, IN_2, IN}), .b(4'b0011), .eq(HHL));  // open: gt, lt
  and and_6 (HHL_t_t_t, HHL, 1'b0);
  and and_7 (HHL_t_t, HHL, 1'b0);
  and and_8 (HHL_t, HHL, 1'b0);

  // Other names for the same wires on the sheet: I_t_t = IN; I_t = IN_2; I = IN_3
endmodule

module SN74LS541DWR (
  input  G1_num,
  input  G2_num,
  input  [7:0] A,
  output [7:0] out_4
);

  wire and_1_out;

  and and_1 (and_1_out, ~G1_num, ~G2_num);  // AND_Gate
  assign out_4 = and_1_out ? A : 8'bz;  // Controlled_Buffer controlled_buffer_1
endmodule

module GR_74HC574TS (
  input  OE_num,
  input  CLK,
  input  [7:0] D,
  output [7:0] Q
);

  wire not_1_out;
  wire [7:0] d_ff_1_q;

  not not_1 (not_1_out, OE_num);
  D_Flip_Flop d_ff_1 (.clk(CLK), .D(D[0]), .Q(d_ff_1_q[0]), .preset(1'b0), .en(1'b1), .reset(1'b0));  // open: Qn
  D_Flip_Flop d_ff_2 (.clk(CLK), .D(D[1]), .Q(d_ff_1_q[1]), .preset(1'b0), .en(1'b1), .reset(1'b0));  // open: Qn
  D_Flip_Flop d_ff_3 (.clk(CLK), .D(D[2]), .Q(d_ff_1_q[2]), .preset(1'b0), .en(1'b1), .reset(1'b0));  // open: Qn
  D_Flip_Flop d_ff_4 (.clk(CLK), .D(D[3]), .Q(d_ff_1_q[3]), .preset(1'b0), .en(1'b1), .reset(1'b0));  // open: Qn
  D_Flip_Flop d_ff_5 (.clk(CLK), .D(D[4]), .Q(d_ff_1_q[4]), .preset(1'b0), .en(1'b1), .reset(1'b0));  // open: Qn
  D_Flip_Flop d_ff_6 (.clk(CLK), .D(D[5]), .Q(d_ff_1_q[5]), .preset(1'b0), .en(1'b1), .reset(1'b0));  // open: Qn
  D_Flip_Flop d_ff_7 (.clk(CLK), .D(D[6]), .Q(d_ff_1_q[6]), .preset(1'b0), .en(1'b1), .reset(1'b0));  // open: Qn
  D_Flip_Flop d_ff_8 (.clk(CLK), .D(D[7]), .Q(d_ff_1_q[7]), .preset(1'b0), .en(1'b1), .reset(1'b0));  // open: Qn
  assign Q = not_1_out ? d_ff_1_q : 8'bz;  // Controlled_Buffer controlled_buffer_1
endmodule

module XL74LS138 (
  input  A,
  input  B,
  input  C,
  input  G1,
  input  G2A_num,
  input  G2B_num,
  output [7:0] Y_num
);

  wire buffer_1_out, buffer_2_out, buffer_3_out, buffer_4_out, nand_1_out, nand_2_out, nand_3_out,
       nand_4_out, nand_5_out, nand_6_out, nand_7_out, nand_8_out, nand_9_out, not_1_out, not_2_out,
       not_3_out, not_4_out, not_5_out;

  buf buffer_1 (buffer_1_out, G1);
  buf buffer_2 (buffer_2_out, A);
  buf buffer_3 (buffer_3_out, B);
  buf buffer_4 (buffer_4_out, C);
  nand nand_1 (nand_1_out, buffer_1_out, not_1_out, not_2_out);
  not not_1 (not_1_out, G2A_num);
  not not_2 (not_2_out, G2B_num);
  not not_3 (not_3_out, buffer_2_out);
  not not_4 (not_4_out, buffer_3_out);
  not not_5 (not_5_out, buffer_4_out);
  nand nand_2 (nand_2_out, not_3_out, not_4_out, not_5_out);
  nand nand_3 (nand_3_out, buffer_2_out, not_4_out, not_5_out);
  nand nand_4 (nand_4_out, not_3_out, buffer_3_out, not_5_out);
  nand nand_5 (nand_5_out, buffer_2_out, buffer_3_out, not_5_out);
  nand nand_6 (nand_6_out, not_3_out, not_4_out, buffer_4_out);
  nand nand_7 (nand_7_out, buffer_2_out, not_4_out, buffer_4_out);
  nand nand_8 (nand_8_out, not_3_out, buffer_3_out, buffer_4_out);
  nand nand_9 (nand_9_out, buffer_2_out, buffer_3_out, buffer_4_out);
  nand nand_10 (Y_num[0], ~nand_2_out, ~nand_1_out);  // NAND_Gate
  nand nand_11 (Y_num[1], ~nand_3_out, ~nand_1_out);  // NAND_Gate
  nand nand_12 (Y_num[2], ~nand_4_out, ~nand_1_out);  // NAND_Gate
  nand nand_13 (Y_num[3], ~nand_5_out, ~nand_1_out);  // NAND_Gate
  nand nand_14 (Y_num[4], ~nand_6_out, ~nand_1_out);  // NAND_Gate
  nand nand_15 (Y_num[5], ~nand_7_out, ~nand_1_out);  // NAND_Gate
  nand nand_16 (Y_num[6], ~nand_8_out, ~nand_1_out);  // NAND_Gate
  nand nand_17 (Y_num[7], ~nand_9_out, ~nand_1_out);  // NAND_Gate
endmodule

module SN74LS86ADR (
  input  [3:0] in_1,
  input  [3:0] in_2,
  output [3:0] out_3
);

  assign out_3 = in_1 ^ in_2;  // XOR_Gate xor_1, 4 bits wide
endmodule
